// Logisim project Project2.circ as structural Verilog: 7 circuits, main circuit MIPS32
module MIPS32 (
  input  in_1,
  input  in_2
);

  wire clock_1_out, ctrlidex_1_imm, mips_alu_1_p3, registerfile_1_p4, registerfile_1_p6, registerfile_1_p7,
       undriven;
  wire [31:0] bit_extender_1_out, CTRL_q, ctrlidex_1_ctrl, D_q, idex_1_qa, idex_1_qb, idex_1_qimm,
       incrementer4_1_out_2, mips_alu_1_p4, mipsprogramrom_1_p2, multiplexer_1_out, pc_1_o, register_1_q,
       registerfile_1_p2, registerfile_1_p5, registerfile_1_p10, registerfile_1_p11;

  PC pc_1 (.I(incrementer4_1_out_2), .Reset(in_1), .C(clock_1_out), .Reset2(in_2), .O(pc_1_o));
  Incrementer4 incrementer4_1 (.in_1(pc_1_o), .out_2(incrementer4_1_out_2));
  // Probe on incrementer4_1_out_2
  // MIPSProgramROM mipsprogramrom_1: pin names not known; wires that end beside it: pc_1_o, mipsprogramrom_1_p2
  Register #(.width(32)) register_1 (.D(mipsprogramrom_1_p2), .clk(clock_1_out), .Q(register_1_q));  // open: en, clr
  Clock clock_1 (.out(clock_1_out));
  // RegisterFile registerfile_1: pin names not known; wires that end beside it: register_1_q, registerfile_1_p2, clock_1_out, registerfile_1_p4, registerfile_1_p5, registerfile_1_p6, registerfile_1_p7, registerfile_1_p6, registerfile_1_p7, registerfile_1_p10, registerfile_1_p11
  assign bit_extender_1_out = {{16{register_1_q[15]}}, register_1_q[15:0]};  // Bit_Extender bit_extender_1
  IDEX idex_1 (
    .C(clock_1_out), .DA(registerfile_1_p10), .DB(registerfile_1_p11), .DIMM(bit_extender_1_out),
    .QA(idex_1_qa), .QB(idex_1_qb), .QIMM(idex_1_qimm));
  CtrlIDEX ctrlidex_1 (.D(registerfile_1_p5), .C(clock_1_out), .IMM(ctrlidex_1_imm), .Ctrl(ctrlidex_1_ctrl));
  Multiplexer #(.width(32), .enable("false")) multiplexer_1 (
    .in0(idex_1_qb), .in1(idex_1_qimm), .out(multiplexer_1_out), .sel(ctrlidex_1_imm));
  // Mips_ALU mips_alu_1: pin names not known; wires that end beside it: idex_1_qa, multiplexer_1_out, mips_alu_1_p3, mips_alu_1_p4
  compare compare_1 (.A(idex_1_qa), .B(multiplexer_1_out), .S(undriven));  // open: O
  Register #(.width(32)) D (.D(mips_alu_1_p4), .clk(clock_1_out), .Q(D_q));  // open: en, clr
  Register #(.width(32)) CTRL (.D(ctrlidex_1_ctrl), .clk(clock_1_out), .Q(CTRL_q));  // open: en, clr
  Register #(.width(32)) D_2 (.D(D_q), .clk(clock_1_out), .Q(registerfile_1_p2));  // open: en, clr
  Register #(.width(32)) CTRL_2 (.D(CTRL_q), .clk(clock_1_out));  // open: en, Q, clr

  // Notes on the sheet:
  //   Data?
  //   Write Enabled
  //   Decode
endmodule

module Incrementer4 (
  input  [31:0] in_1,
  output [31:0] out_2
);

  wire bit_extender_1_out, incrementer_1_p2, not_1_out;
  wire [1:1] and_1_out;
  wire [29:0] bit_extender_2_out;

  Bit_Extender #(.in_width(32), .out_width(1), .\type ("zero")) bit_extender_1 (.in(in_1), .out(bit_extender_1_out));
  and and_1 (and_1_out[1], bit_extender_1_out, not_1_out);
  not not_1 (not_1_out, bit_extender_1_out);
  // Incrementer #(.width(1)) incrementer_1: pin names not known; wires that end beside it: and_1_out[1], incrementer_1_p2
  assign bit_extender_2_out = {{29{1'b0}}, incrementer_1_p2};  // Bit_Extender bit_extender_2
  assign out_2 = {bit_extender_2_out, {2{and_1_out[1]}}} ^ in_1;  // XOR_Gate xor_1, 32 bits wide
endmodule

module PC (
  input  [31:0] I,
  input  Reset,
  input  C,
  input  Reset2,
  output [31:0] O
);

  wire not_1_out, or_1_out;
  wire [31:0] multiplexer_1_out;

  Multiplexer #(.width(32), .enable("false")) multiplexer_1 (
    .in0({32{1'b0}}), .in1(I), .out(multiplexer_1_out), .sel(not_1_out));
  not not_1 (not_1_out, Reset);
  or or_1 (or_1_out, C, Reset2);
  Register #(.width(32)) register_1 (.D(multiplexer_1_out), .clk(or_1_out), .Q(O));  // open: en, clr
endmodule

module IDEX (
  input  C,
  input  [31:0] DA,
  input  [31:0] DB,
  input  [31:0] DIMM,
  output [31:0] QA,
  output [31:0] QB,
  output [31:0] QIMM
);

  Register #(.width(32)) register_1 (.D(DA), .clk(C), .Q(QA));  // open: en, clr
  Register #(.width(32)) register_2 (.D(DB), .clk(C), .Q(QB));  // open: en, clr
  Register #(.width(32)) register_3 (.D(DIMM), .clk(C), .Q(QIMM));  // open: en, clr
endmodule

module CtrlIDEX (
  input  [31:0] D,
  input  C,
  output IMM,
  output [31:0] Ctrl
);

  wire and_1_out, and_2_out, and_3_out, and_4_out, not_1_out, not_2_out, not_3_out, not_4_out, not_5_out,
       not_6_out, not_7_out, not_8_out, not_9_out, not_10_out, not_11_out, not_12_out;

  Register #(.width(32)) register_1 (.D(D), .clk(C), .Q(Ctrl));  // open: en, clr
  not not_1 (not_1_out, Ctrl[31]);
  not not_2 (not_2_out, Ctrl[30]);
  not not_3 (not_3_out, Ctrl[28]);
  not not_4 (not_4_out, Ctrl[31]);
  not not_5 (not_5_out, Ctrl[30]);
  not not_6 (not_6_out, Ctrl[28]);
  not not_7 (not_7_out, Ctrl[31]);
  not not_8 (not_8_out, Ctrl[30]);
  not not_9 (not_9_out, Ctrl[27]);
  not not_10 (not_10_out, Ctrl[31]);
  not not_11 (not_11_out, Ctrl[30]);
  not not_12 (not_12_out, Ctrl[26]);
  and and_1 (and_1_out, not_1_out, not_2_out, Ctrl[29], not_3_out, Ctrl[26]);
  and and_2 (and_2_out, not_4_out, not_5_out, Ctrl[29], not_6_out, Ctrl[27]);
  and and_3 (and_3_out, not_7_out, not_8_out, Ctrl[29], Ctrl[28], not_9_out);
  and and_4 (and_4_out, not_10_out, not_11_out, Ctrl[29], Ctrl[28], not_12_out);
  or or_1 (IMM, and_1_out, and_2_out, and_3_out, and_4_out);
endmodule

module test (
  input  [7:0] in_1,
  input  [7:0] in_2
);

  wire comparator_1_eq, comparator_1_gt, comparator_1_lt;

  Comparator comparator_1 (.a(in_1), .b(in_2), .gt(comparator_1_gt), .eq(comparator_1_eq), .lt(comparator_1_lt));
endmodule

module compare (
  input  [31:0] A,
  input  [31:0] B,
  input  S,
  output [31:0] O
);

  wire comparator_1_eq, comparator_2_eq, multiplexer_1_out;

  Comparator #(.width(32)) comparator_1 (.a(A), .b(B), .eq(comparator_1_eq));  // open: gt, lt
  Comparator #(.width(32), .mode("unsigned")) comparator_2 (.a(A), .b(B), .eq(comparator_2_eq));  // open: gt, lt
  Multiplexer #(.enable("false")) multiplexer_1 (
    .in0(comparator_1_eq), .in1(comparator_2_eq), .out(multiplexer_1_out), .sel(S));
  assign O = {{31{1'b0}}, multiplexer_1_out};  // Bit_Extender bit_extender_1

  // Notes on the sheet:
  //   signed
  //   unsigned
endmodule
